# Fritzing sketch ClueDelivery_LCD (saved by Fritzing 0.9.3b)

parts:
  Part1 = Arduino Uno (Rev3)
  J1 = female pin header, 4 pins [form="♀ (female)"]

nets:
  N1: Part1.A4/SDA, J1.pin3
  N2: Part1.A5/SCL, J1.pin4
  N3: Part1.5V, J1.pin1
  N4: Part1.GND, J1.pin2

notes:
  VCC <-> 5V
  GND <-> GND
  SDA <-> A4
  SCL <-> A5
  LCD 2004 with PCF8574 I2C backpack
  Arduino UNO/Nano etc.
