# Fritzing sketch ESP32 W5500 Wired Ethernet (saved by Fritzing 0.9.4)

parts:
  J1 = female pin header, 5 pins [form="♀ (female)"]
  J2 = female pin header, 5 pins [form="♀ (female)"]
  U1 = ESP32S-HiLetgo [part_number=ESP32S-HiLetgo]

nets:
  N1: J1.pin1, U1.GPIO18
  N2: J1.pin2, U1.GPIO5
  N3: J1.pin3, U1.GPIO23
  N4: J1.pin4, U1.GPIO19
  N5: J1.pin5, U1.3.3
  N6: J2.pin3, U1.GPIO26
  N7: J2.pin4, U1.GND
  N8: J2.pin5, U1.VIN

notes:
  SPI connection from ESP32 to W5500
  GPIO23 <> MOSI
  GPIO19 <> MISO
  GPIO18 <> CLK
  GPIO5 <> CS
  GPIO 26 <> RESET
  Pinout of W5500
  NC CLK
  INT CS
  RST MOSI
  GND MISO
  5V 3.3V

custom parts:
  ESP32S-HiLetgo: HiLetgo ESP-WROOM-32 ESP32 ESP-32S Development Board 2.4GHz Dual-Mode WiFi + Bluetooth Dual Cores Microcontroller The ESP32 integrated with Antenna switches, RF Balun, power amplifiers, low-noise amplifiers, filters, and management modules, and the entire solution occupies the least area of PCB. 2.4 GHz Wi-Fi plus Bluetooth dual-mode chip, with TSMC Ultra-low power consumption 40nm technology,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
