# Fritzing sketch WemosD1Mini_DualShaftStepper (saved by Fritzing 0.9.3b)

parts:
  M2 = Dual-shaft Bipolar Stepper Motor
  WeMos_D1_Mini2 = WeMos D1 Mini

nets:
  N1: M2.pin_1, WeMos_D1_Mini2.D1
  N2: M2.pin_2, WeMos_D1_Mini2.D2
  N3: M2.pin_3, WeMos_D1_Mini2.D3
  N4: M2.pin_4, WeMos_D1_Mini2.D4
  N5: M2.pin_5, WeMos_D1_Mini2.D5
  N6: M2.pin_6, WeMos_D1_Mini2.D6
  N7: M2.pin_7, WeMos_D1_Mini2.D7
  N8: M2.pin_8, WeMos_D1_Mini2.D8

notes:
  BKA30D-R5 Dual-Shaft Stepper Motor connected to Wemos D1 pins as follows:
  { D1, D2 } { D5, D6 }
  { D3, D4 } { D7, D8 }
  Wemos D1 running local web server

custom parts:
  Dual-shaft Bipolar Stepper Motor: 2x4 wire stepper motors in a single unit, as often used in vehicle instrument control panels e.g.BKA30D-R5
